# Fritzing sketch schaltung (saved by Fritzing 0.9.3b)
breadboards: 1

parts:
  IC1 = L293D [package=THT]
  BAT1 = Battery Holders [package=battery-aa]
  BAT2 = Battery Holders [package=battery-aa]
  BAT3 = Battery Holders [package=battery-aa]
  M1 = DC Motor
  M2 = DC Motor
  Part1 = Arduino Nano (Rev3.0) (ICSP)
  J1 = Piezo Speaker
  R1 = Temperature Sensor (Thermistor) [thermistor_type=NTC package=THT]
  LED1 = LEDs [package=led10mm]
  R2 = Trimmer Potentiometer [maximum_resistance=10kΩ package=THT]
  R3 = Resistor [tolerance=±5% resistance=220 package="0402 [SMD]"]
  R4 = Resistor [tolerance=±5% resistance=350 package="0402 [SMD]"]
  LED3 = LED - 5mm [color="Red (633nm)" package="5 mm [THT]"]  # not connected
  LED4 = LED - 5mm [color="Red (633nm)" package="5 mm [THT]"]

nets:
  N1: IC1.Enable_1, IC1.+Vmotor, IC1.Enable_2, IC1.+V, BAT3.+, R1.pin_0
  N2: IC1.In_1, Part1.D10
  N3: IC1.Out_1_(_Controlled_by_Enable_1_), M2.pin_2
  N4: IC1.0V, BAT1.-, J1.pin1, LED1.A, R2.wiper, R4.Pin_0
  N5: IC1.Out_2_(_Controlled_by_Enable_1_), M2.pin_1
  N6: IC1.In_2, Part1.D9
  N7: IC1.In_3, Part1.D5
  N8: IC1.Out_3_(_Controlled_by_Enable_2_), M1.pin_1
  N9: IC1.In_4, M1.pin_2, Part1.D6
  N10: BAT1.+, BAT2.-
  N11: BAT2.+, BAT3.-
  N12: Part1.D7, R3.Pin_1
  N13: Part1.D8, LED4.anode
  N14: Part1.D11/MOSI, J1.pin2
  N15: R1.pin_1, R2.leg2
